// Logisim project newVersion.circ as structural Verilog: 12 circuits, main circuit main
module main (
  input  reset,
  output [31:0] out_2,
  output out_3,
  output [4:0] out_4,
  output [31:0] out_5,
  output out_6,
  output [4:0] out_7,
  output [31:0] out_8
);

  wire clk;
  wire [2:0] jump;
  wire [3:0] alu_1_alu_type;
  wire [4:0] rd, rs, rt, shamt;
  wire [5:0] func, op;
  wire [15:0] _16;
  wire [25:0] _26;
  wire [31:0] _29data, alu_out, dm_out, npc_1_out_7, pc4, pc_1_do, rsdata, rtdata;

  Clock clock_1 (.out(clk));
  PC pc_1 (.DI(npc_1_out_7), .reset(reset), .clk(clk), .DO(pc_1_do));
  // Probe on npc_1_out_7
  PC4 pc4_1 (.in_1(pc_1_do), .out_2(pc4));
  Jump_type jump_type_1 (.func(func), .op(op), .out_3(jump));
  IFU ifu_1 (
    .PC(pc_1_do), .func(func), .shamt(shamt), .rd(rd), .rt(rt), .rs(rs), .op(op), .imm26(_26), .imm16(_16),
    .instr(out_2));
  NPC npc_1 (.imm26(_26), .in_2(rsdata), .in_3(rtdata), .imm16(_16), .pc4(pc4), .jump_type(jump), .out_7(npc_1_out_7));
  grf grf_1 (
    .func(func), .op(op), .rt(rt), .rd(rd), .alu_out({alu_out[31:7], out_7, alu_out[1:0]}), .dm_out(dm_out),
    .jump(jump), .out_8(out_4), .out_9(out_5), .wrt(out_3));
  GRF grf_2 (
    .A1(rs), .A2(rt), .A3(out_4), .RD1(rsdata), .RD2(rtdata), .WD(out_5), .clk(clk), .reset(reset),
    .WE(out_3), ._29data(_29data));
  dm dm_1 (.func(func), .op(op), .pc4(pc4), .rt(rtdata), .jump(jump), .is_sw(out_6), .RegData(out_8));
  alu alu_1 (.func(func), .op(op), .alu_type(alu_1_alu_type));
  ALU alu_2 (
    .rs_data(rsdata), .rt_data(rtdata), .imm16(_16), .alu_type(alu_1_alu_type),
    .out_5({alu_out[31:7], out_7, alu_out[1:0]}));
  DM dm_2 (.addr(out_7), .en(out_6), .data(out_8), .rst(reset), .clk(clk), .out_6(dm_out));

  // Other names for the same wires on the sheet: alu_out[6:2] = out_7; MemAddr[4:0] = out_7; instr[31:0] = out_2;
  //   Memdata[31:0] = out_8; MemWrite = out_6; RegAddr[4:0] = out_4; RegData[31:0] = out_5; RegWrite = out_3
endmodule

module PC (
  input  [31:0] DI,
  input  reset,
  input  clk,
  output [31:0] DO
);

  Register #(.width(32)) register_1 (.D(DI), .Q(DO), .clk(clk), .clr(reset));  // open: en
endmodule

module PC4 (
  input  [31:0] in_1,
  output [31:0] out_2
);

  Adder #(.width(32)) adder_1 (.a(in_1), .b(32'h4), .out(out_2));  // open: cin, cout
endmodule

module IFU (
  input  [31:0] PC,
  output [5:0] func,
  output [4:0] shamt,
  output [4:0] rd,
  output [4:0] rt,
  output [4:0] rs,
  output [5:0] op,
  output [25:0] imm26,
  output [15:0] imm16,
  output [31:0] instr
);

  ROM #(.addrWidth(5), .dataWidth(32)) rom_1 (
    .addr(PC[6:2]), .data({instr[31:26], imm26[25:16], imm16[15:6], func}));  // open: sel

  assign imm16[5:0] = func;
  assign imm26[15:0] = {imm16[15:6], func};
  assign instr[25:0] = {imm26[25:16], imm16[15:6], func};
  assign op = instr[31:26];
  assign rd = imm16[15:11];
  assign rs = imm26[25:21];
  assign rt = imm26[20:16];
  assign shamt = imm16[10:6];

  // Notes on the sheet:
  //   contents of rom_1 (hex, n*v repeats v):
  //   34010001 3c01ffff 3421fffe 11025 34030000 d0220001
endmodule

module GRF (
  input  clk,
  input  reset,
  input  WE,
  input  [31:0] WD,
  input  [4:0] A3,
  input  [4:0] A1,
  input  [4:0] A2,
  output [31:0] RD1,
  output [31:0] RD2,
  output [31:0] _29data
);

  wire and_1_out, and_2_out, and_3_out, and_4_out, and_5_out, and_6_out, and_7_out, and_8_out, and_9_out,
       and_10_out, and_11_out, and_12_out, and_13_out, and_14_out, and_15_out, and_16_out, and_17_out,
       and_18_out, and_19_out, and_20_out, and_21_out, and_22_out, and_23_out, and_24_out, and_25_out,
       and_26_out, and_27_out, and_28_out, and_29_out, and_30_out, and_31_out;
  wire [31:0] R0out, R1in, R1out, R2in, R2out, R3in, R3out, R4in, R4out, R5in, R5out, R6in, R6out, R7in,
       R7out, R8in, R8out, R9in, R9out, R10in, R10out, R11in, R11out, R12in, R12out, R13in, R13out, R14in,
       R14out, R15in, R15out, R16in, R16out, R17in, R17out, R18in, R18out, R19in, R19out, R20in, R20out,
       R21in, R21out, R22in, R22out, R23in, R23out, R24in, R24out, R25in, R25out, R26in, R26out, R27in,
       R27out, R28in, R28out, R29in, R30in, R30out, R31in, R31out;

  buf and_1 (and_1_out, clk);  // AND_Gate
  buf and_2 (and_2_out, clk);  // AND_Gate
  buf and_3 (and_3_out, clk);  // AND_Gate
  Register #(.width(32)) register_1 (.D({32{1'b0}}), .Q(R0out), .clk(clk), .clr(reset));  // open: en
  Register #(.width(32)) register_2 (.D(R8in), .Q(R8out), .clk(and_1_out), .clr(reset));  // open: en
  Register #(.width(32)) register_3 (.D(R16in), .Q(R16out), .clk(and_2_out), .clr(reset));  // open: en
  Register #(.width(32)) register_4 (.D(R24in), .Q(R24out), .clk(and_3_out), .clr(reset));  // open: en
  Register #(.width(32)) register_5 (.D(R1in), .Q(R1out), .clk(and_4_out), .clr(reset));  // open: en
  buf and_4 (and_4_out, clk);  // AND_Gate
  Register #(.width(32)) register_6 (.D(R9in), .Q(R9out), .clk(and_5_out), .clr(reset));  // open: en
  buf and_5 (and_5_out, clk);  // AND_Gate
  Register #(.width(32)) register_7 (.D(R17in), .Q(R17out), .clk(and_6_out), .clr(reset));  // open: en
  buf and_6 (and_6_out, clk);  // AND_Gate
  Register #(.width(32)) register_8 (.D(R25in), .Q(R25out), .clk(and_7_out), .clr(reset));  // open: en
  buf and_7 (and_7_out, clk);  // AND_Gate
  // Probe on nothing
  buf and_8 (and_8_out, clk);  // AND_Gate
  buf and_9 (and_9_out, clk);  // AND_Gate
  buf and_10 (and_10_out, clk);  // AND_Gate
  buf and_11 (and_11_out, clk);  // AND_Gate
  Register #(.width(32)) register_9 (.D(R2in), .Q(R2out), .clk(and_8_out), .clr(reset));  // open: en
  Register #(.width(32)) register_10 (.D(R10in), .Q(R10out), .clk(and_9_out), .clr(reset));  // open: en
  Register #(.width(32)) register_11 (.D(R18in), .Q(R18out), .clk(and_10_out), .clr(reset));  // open: en
  Register #(.width(32)) register_12 (.D(R26in), .Q(R26out), .clk(and_11_out), .clr(reset));  // open: en
  Multiplexer #(.select(5), .width(32), .enable("false")) multiplexer_1 (
    .in0(R0out), .in1(R1out), .in2(R2out), .in3(R3out), .in4(R4out), .in5(R5out), .in6(R6out), .in7(R7out),
    .in8(R8out), .in9(R9out), .in10(R10out), .in11(R11out), .in12(R12out), .in13(R13out), .in14(R14out),
    .in15(R15out), .in16(R16out), .in17(R17out), .in18(R18out), .in19(R19out), .in20(R20out), .in21(R21out),
    .in22(R22out), .in23(R23out), .in24(R24out), .in25(R25out), .in26(R26out), .in27(R27out), .in28(R28out),
    .in29(_29data), .in30(R30out), .in31(R31out), .out(RD1), .sel(A1));
  Register #(.width(32)) register_13 (.D(R3in), .Q(R3out), .clk(and_12_out), .clr(reset));  // open: en
  buf and_12 (and_12_out, clk);  // AND_Gate
  Register #(.width(32)) register_14 (.D(R11in), .Q(R11out), .clk(and_13_out), .clr(reset));  // open: en
  buf and_13 (and_13_out, clk);  // AND_Gate
  Register #(.width(32)) register_15 (.D(R19in), .Q(R19out), .clk(and_14_out), .clr(reset));  // open: en
  buf and_14 (and_14_out, clk);  // AND_Gate
  Register #(.width(32)) register_16 (.D(R27in), .Q(R27out), .clk(and_15_out), .clr(reset));  // open: en
  buf and_15 (and_15_out, clk);  // AND_Gate
  Demultiplexer #(.select(5), .width(32), .tristate("true")) demultiplexer_1 (
    .out1(R1in), .out2(R2in), .out3(R3in), .out4(R4in), .out5(R5in), .out6(R6in), .out7(R7in), .out8(R8in),
    .out9(R9in), .out10(R10in), .out11(R11in), .out12(R12in), .out13(R13in), .out14(R14in), .out15(R15in),
    .out16(R16in), .out17(R17in), .out18(R18in), .out19(R19in), .out20(R20in), .out21(R21in), .out22(R22in),
    .out23(R23in), .out24(R24in), .out25(R25in), .out26(R26in), .out27(R27in), .out28(R28in), .out29(R29in),
    .out30(R30in), .out31(R31in), .in(WD), .sel(A3), .en(WE));  // open: out0
  buf and_16 (and_16_out, clk);  // AND_Gate
  buf and_17 (and_17_out, clk);  // AND_Gate
  buf and_18 (and_18_out, clk);  // AND_Gate
  buf and_19 (and_19_out, clk);  // AND_Gate
  Register #(.width(32)) register_17 (.D(R4in), .Q(R4out), .clk(and_16_out), .clr(reset));  // open: en
  Register #(.width(32)) register_18 (.D(R12in), .Q(R12out), .clk(and_17_out), .clr(reset));  // open: en
  Register #(.width(32)) register_19 (.D(R20in), .Q(R20out), .clk(and_18_out), .clr(reset));  // open: en
  Register #(.width(32)) register_20 (.D(R28in), .Q(R28out), .clk(and_19_out), .clr(reset));  // open: en
  Register #(.width(32)) register_21 (.D(R5in), .Q(R5out), .clk(and_20_out), .clr(reset));  // open: en
  buf and_20 (and_20_out, clk);  // AND_Gate
  Register #(.width(32)) register_22 (.D(R13in), .Q(R13out), .clk(and_21_out), .clr(reset));  // open: en
  buf and_21 (and_21_out, clk);  // AND_Gate
  Register #(.width(32)) register_23 (.D(R21in), .Q(R21out), .clk(and_22_out), .clr(reset));  // open: en
  buf and_22 (and_22_out, clk);  // AND_Gate
  Register #(.width(32)) register_24 (.D(R29in), .Q(_29data), .clk(and_23_out), .clr(reset));  // open: en
  buf and_23 (and_23_out, clk);  // AND_Gate
  Multiplexer #(.select(5), .width(32), .enable("false")) multiplexer_2 (
    .in0(R0out), .in1(R1out), .in2(R2out), .in3(R3out), .in4(R4out), .in5(R5out), .in6(R6out), .in7(R7out),
    .in8(R8out), .in9(R9out), .in10(R10out), .in11(R11out), .in12(R12out), .in13(R13out), .in14(R14out),
    .in15(R15out), .in16(R16out), .in17(R17out), .in18(R18out), .in19(R19out), .in20(R20out), .in21(R21out),
    .in22(R22out), .in23(R23out), .in24(R24out), .in25(R25out), .in26(R26out), .in27(R27out), .in28(R28out),
    .in29(_29data), .in30(R30out), .in31(R31out), .out(RD2), .sel(A2));
  buf and_24 (and_24_out, clk);  // AND_Gate
  buf and_25 (and_25_out, clk);  // AND_Gate
  buf and_26 (and_26_out, clk);  // AND_Gate
  buf and_27 (and_27_out, clk);  // AND_Gate
  Register #(.width(32)) register_25 (.D(R6in), .Q(R6out), .clk(and_24_out), .clr(reset));  // open: en
  Register #(.width(32)) register_26 (.D(R14in), .Q(R14out), .clk(and_25_out), .clr(reset));  // open: en
  Register #(.width(32)) register_27 (.D(R22in), .Q(R22out), .clk(and_26_out), .clr(reset));  // open: en
  Register #(.width(32)) register_28 (.D(R30in), .Q(R30out), .clk(and_27_out), .clr(reset));  // open: en
  Register #(.width(32)) register_29 (.D(R7in), .Q(R7out), .clk(and_28_out), .clr(reset));  // open: en
  buf and_28 (and_28_out, clk);  // AND_Gate
  Register #(.width(32)) register_30 (.D(R15in), .Q(R15out), .clk(and_29_out), .clr(reset));  // open: en
  buf and_29 (and_29_out, clk);  // AND_Gate
  Register #(.width(32)) register_31 (.D(R23in), .Q(R23out), .clk(and_30_out), .clr(reset));  // open: en
  buf and_30 (and_30_out, clk);  // AND_Gate
  Register #(.width(32)) register_32 (.D(R31in), .Q(R31out), .clk(and_31_out), .clr(reset));  // open: en
  buf and_31 (and_31_out, clk);  // AND_Gate

  // Other names for the same wires on the sheet: R29out[31:0] = _29data
endmodule

module DM (
  input  [4:0] addr,
  input  en,
  input  [31:0] data,
  input  rst,
  input  clk,
  output [31:0] out_6
);

  wire and_1_out;

  buf and_1 (and_1_out, clk);  // AND_Gate
  RAM #(.addrWidth(5), .dataWidth(32), .bus("separate")) ram_1 (
    .addr(addr), .din(data), .data(out_6), .str(en), .clk(and_1_out), .clr(rst));  // open: sel, ld
endmodule

module ALU (
  input  [31:0] rs_data,
  input  [31:0] rt_data,
  input  [15:0] imm16,
  input  [3:0] alu_type,
  output [31:0] out_5
);

  wire [31:0] adder_1_out, adder_2_out, bit_extender_1_out, bit_extender_2_out, or_1_out, or_2_out,
       shifter_1_out, subtractor_1_out, xor_1_out;

  assign bit_extender_1_out = {{16{1'b0}}, imm16};  // Bit_Extender bit_extender_1
  assign bit_extender_2_out = {{16{imm16[15]}}, imm16};  // Bit_Extender bit_extender_2
  Shifter #(.width(32), .shift("lr")) shifter_1 (.in(rs_data), .\dist (5'b00001), .out(shifter_1_out));
  assign xor_1_out = shifter_1_out ^ rs_data;  // XOR_Gate xor_1, 32 bits wide
  Adder #(.width(32)) adder_1 (.a(rs_data), .b(rt_data), .out(adder_1_out));  // open: cin, cout
  Subtractor #(.width(32)) subtractor_1 (.a(rs_data), .b(rt_data), .out(subtractor_1_out));  // open: bin, bout
  assign or_1_out = rs_data | bit_extender_1_out;  // OR_Gate or_1, 32 bits wide
  Adder #(.width(32)) adder_2 (.a(rs_data), .b(bit_extender_2_out), .out(adder_2_out));  // open: cin, cout
  assign or_2_out = rs_data | rt_data;  // OR_Gate or_2, 32 bits wide
  Multiplexer #(.select(4), .width(32)) multiplexer_1 (
    .in0({32{1'b0}}), .in1(adder_1_out), .in2(subtractor_1_out), .in3(or_1_out), .in4({imm16, {16{1'b0}}}),
    .in5(adder_2_out), .in6(xor_1_out), .in7(or_2_out), .out(out_5), .sel(alu_type));  // open: in8, in9, in10, in11, in12, in13, in14, in15, en
endmodule

module alu (
  input  [5:0] func,
  input  [5:0] op,
  output [3:0] alu_type
);

  wire comparator_1_eq, comparator_2_eq, comparator_3_eq, comparator_4_eq, comparator_5_eq, comparator_6_eq,
       comparator_7_eq, comparator_8_eq, comparator_9_eq, comparator_10_eq;
  wire [3:0] multiplexer_1_out, multiplexer_2_out, multiplexer_3_out, multiplexer_4_out, multiplexer_5_out,
       multiplexer_6_out, multiplexer_7_out, multiplexer_8_out, multiplexer_9_out;

  Comparator #(.width(6), .mode("unsigned")) comparator_1 (
    .a(func), .b(6'b100000), .eq(comparator_1_eq));  // open: gt, lt
  Comparator #(.width(6), .mode("unsigned")) comparator_2 (
    .a(func), .b(6'b100010), .eq(comparator_2_eq));  // open: gt, lt
  Comparator #(.width(6), .mode("unsigned")) comparator_3 (
    .a(func), .b(6'b110001), .eq(comparator_3_eq));  // open: gt, lt
  Comparator #(.width(6), .mode("unsigned")) comparator_4 (
    .a(func), .b(6'b100101), .eq(comparator_4_eq));  // open: gt, lt
  Comparator #(.width(6), .mode("unsigned")) comparator_5 (
    .a(op), .b(6'b001101), .eq(comparator_5_eq));  // open: gt, lt
  Comparator #(.width(6), .mode("unsigned")) comparator_6 (
    .a(op), .b(6'b100011), .eq(comparator_6_eq));  // open: gt, lt
  Comparator #(.width(6), .mode("unsigned")) comparator_7 (
    .a(op), .b(6'b101011), .eq(comparator_7_eq));  // open: gt, lt
  Comparator #(.width(6), .mode("unsigned")) comparator_8 (
    .a(op), .b(6'b001111), .eq(comparator_8_eq));  // open: gt, lt
  Comparator #(.width(6), .mode("unsigned")) comparator_9 (
    .a(op), .b(6'b110100), .eq(comparator_9_eq));  // open: gt, lt
  Multiplexer #(.width(4)) multiplexer_1 (
    .in0(4'b0000), .in1(4'b0001), .out(multiplexer_1_out), .sel(comparator_1_eq));  // open: en
  Multiplexer #(.width(4)) multiplexer_2 (
    .in0(4'b0000), .in1(4'b0011), .out(multiplexer_2_out), .sel(comparator_5_eq));  // open: en
  Multiplexer #(.width(4)) multiplexer_3 (
    .in0(multiplexer_2_out), .in1(4'b0101), .out(multiplexer_3_out), .sel(comparator_6_eq));  // open: en
  Multiplexer #(.width(4)) multiplexer_4 (
    .in0(multiplexer_3_out), .in1(4'b0101), .out(multiplexer_4_out), .sel(comparator_7_eq));  // open: en
  Multiplexer #(.width(4)) multiplexer_5 (
    .in0(multiplexer_4_out), .in1(4'b0100), .out(multiplexer_5_out), .sel(comparator_8_eq));  // open: en
  Multiplexer #(.width(4)) multiplexer_6 (
    .in0(multiplexer_5_out), .in1(4'b0101), .out(multiplexer_6_out), .sel(comparator_9_eq));  // open: en
  Multiplexer #(.width(4)) multiplexer_7 (
    .in0(multiplexer_1_out), .in1(4'b0010), .out(multiplexer_7_out), .sel(comparator_2_eq));  // open: en
  Multiplexer #(.width(4)) multiplexer_8 (
    .in0(multiplexer_7_out), .in1(4'b0110), .out(multiplexer_8_out), .sel(comparator_3_eq));  // open: en
  Multiplexer #(.width(4)) multiplexer_9 (
    .in0(multiplexer_8_out), .in1(4'b0111), .out(multiplexer_9_out), .sel(comparator_4_eq));  // open: en
  Multiplexer #(.width(4)) multiplexer_10 (
    .in0(multiplexer_6_out), .in1(multiplexer_9_out), .out(alu_type), .sel(comparator_10_eq));  // open: en
  Comparator #(.width(6), .mode("unsigned")) comparator_10 (
    .a(op), .b({6{1'b0}}), .eq(comparator_10_eq));  // open: gt, lt
endmodule

// jump
module Jump_type (
  input  [5:0] func,
  input  [5:0] op,
  output [2:0] out_3
);

  wire and_1_out, comparator_1_eq, comparator_2_eq, comparator_3_eq, comparator_4_eq;
  wire [2:0] multiplexer_1_out, multiplexer_2_out;

  Comparator #(.width(6), .mode("unsigned")) comparator_1 (
    .a(op), .b({6{1'b0}}), .eq(comparator_1_eq));  // open: gt, lt
  Comparator #(.width(6), .mode("unsigned")) comparator_2 (
    .a(op), .b(6'b000100), .eq(comparator_2_eq));  // open: gt, lt
  Comparator #(.width(6), .mode("unsigned")) comparator_3 (
    .a(func), .b(6'b001001), .eq(comparator_3_eq));  // open: gt, lt
  Comparator #(.width(6), .mode("unsigned")) comparator_4 (
    .a(op), .b(6'b110110), .eq(comparator_4_eq));  // open: gt, lt
  Multiplexer #(.width(3)) multiplexer_1 (
    .in0(3'b000), .in1(3'b001), .out(multiplexer_1_out), .sel(comparator_2_eq));  // open: en
  and and_1 (and_1_out, comparator_1_eq, comparator_3_eq);
  Multiplexer #(.width(3)) multiplexer_2 (
    .in0(multiplexer_1_out), .in1(3'b010), .out(multiplexer_2_out), .sel(and_1_out));  // open: en
  Multiplexer #(.width(3)) multiplexer_3 (
    .in0(multiplexer_2_out), .in1(3'b011), .out(out_3), .sel(comparator_4_eq));  // open: en
endmodule

module dm (
  input  [5:0] func,
  input  [5:0] op,
  input  [31:0] pc4,
  input  [31:0] rt,
  input  [2:0] jump,
  output is_sw,
  output [31:0] RegData
);

  wire comparator_1_eq, comparator_2_eq, comparator_3_eq, comparator_4_eq;
  wire [31:0] multiplexer_1_out;

  Comparator #(.width(6), .mode("unsigned")) comparator_1 (
    .a(op), .b(6'b101011), .eq(comparator_1_eq));  // open: gt, lt
  Comparator #(.width(6), .mode("unsigned")) comparator_2 (
    .a(op), .b(6'b110110), .eq(comparator_2_eq));  // open: gt, lt
  Comparator #(.width(6), .mode("unsigned")) comparator_3 (
    .a(op), .b(6'b110100), .eq(comparator_3_eq));  // open: gt, lt
  Comparator #(.width(3), .mode("unsigned")) comparator_4 (.a(jump), .b(3'b011), .eq(comparator_4_eq));  // open: gt, lt
  or or_1 (is_sw, comparator_1_eq, comparator_2_eq, comparator_3_eq);
  Multiplexer #(.width(32)) multiplexer_1 (
    .in0(rt), .in1(pc4), .out(multiplexer_1_out), .sel(comparator_4_eq));  // open: en
  Multiplexer #(.width(32)) multiplexer_2 (
    .in0(multiplexer_1_out), .in1({rt[7:0], rt[7:0], rt[7:0], rt[7:0]}), .out(RegData), .sel(comparator_3_eq));  // open: en

  // Other names for the same wires on the sheet: _7_0[7:0] = rt[7:0]
endmodule

module NPC (
  input  [25:0] imm26,
  input  [31:0] in_2,
  input  [31:0] in_3,
  input  [15:0] imm16,
  input  [31:0] pc4,
  input  [2:0] jump_type,
  output [31:0] out_7
);

  wire comparator_1_eq, comparator_2_eq, multiplexer_1_out;
  wire [31:0] adder_1_out, bit_extender_1_out, multiplexer_2_out, subtractor_1_out;

  Comparator #(.width(32), .mode("unsigned")) comparator_1 (.a(in_2), .b(in_3), .eq(comparator_1_eq));  // open: gt, lt
  Subtractor #(.width(32)) subtractor_1 (.a(pc4), .b(32'h4), .out(subtractor_1_out));  // open: bin, bout
  assign bit_extender_1_out = {{14{imm16[15]}}, {imm16, 2'b00}};  // Bit_Extender bit_extender_1
  Multiplexer #(.select(3)) multiplexer_1 (
    .in0(1'b0), .in1(comparator_1_eq), .out(multiplexer_1_out), .sel(jump_type));  // open: in2, in3, in4, in5, in6, in7, en
  Adder #(.width(32)) adder_1 (.a(bit_extender_1_out), .b(pc4), .out(adder_1_out));  // open: cin, cout
  Multiplexer #(.width(32)) multiplexer_2 (
    .in0(pc4), .in1(adder_1_out), .out(multiplexer_2_out), .sel(multiplexer_1_out));  // open: en
  Multiplexer #(.width(32)) multiplexer_3 (
    .in0(multiplexer_2_out), .in1({subtractor_1_out[31:28], imm26, 2'b00}), .out(out_7), .sel(comparator_2_eq));  // open: en
  Comparator #(.width(3), .mode("unsigned")) comparator_2 (
    .a(3'b011), .b(jump_type), .eq(comparator_2_eq));  // open: gt, lt
endmodule

module grf (
  input  [5:0] func,
  input  [5:0] op,
  input  [4:0] rt,
  input  [4:0] rd,
  input  [31:0] alu_out,
  input  [31:0] dm_out,
  input  [2:0] jump,
  output [4:0] out_8,
  output [31:0] out_9,
  output wrt
);

  wire and_1_out, and_2_out, and_3_out, comparator_1_eq, comparator_2_eq, comparator_3_eq, comparator_4_eq,
       comparator_5_eq, comparator_6_eq, not_1_out, not_2_out, not_3_out;
  wire [4:0] multiplexer_1_out;

  Comparator #(.width(6), .mode("unsigned")) comparator_1 (
    .a(func), .b({6{1'b0}}), .eq(comparator_1_eq));  // open: gt, lt
  Comparator #(.width(6), .mode("unsigned")) comparator_2 (
    .a(op), .b({6{1'b0}}), .eq(comparator_2_eq));  // open: gt, lt
  Comparator #(.width(6), .mode("unsigned")) comparator_3 (
    .a(op), .b(6'b100011), .eq(comparator_3_eq));  // open: gt, lt
  Comparator #(.width(6), .mode("unsigned")) comparator_4 (
    .a(op), .b(6'b101011), .eq(comparator_4_eq));  // open: gt, lt
  not not_1 (not_1_out, comparator_4_eq);
  Comparator #(.width(6), .mode("unsigned")) comparator_5 (
    .a(op), .b(6'b110100), .eq(comparator_5_eq));  // open: gt, lt
  not not_2 (not_2_out, comparator_5_eq);
  Comparator #(.width(3), .mode("unsigned")) comparator_6 (.a(jump), .b(3'b000), .eq(comparator_6_eq));  // open: gt, lt
  and and_1 (and_1_out, comparator_1_eq, comparator_2_eq);
  Multiplexer #(.width(5)) multiplexer_1 (
    .in0(rt), .in1(rd), .out(multiplexer_1_out), .sel(comparator_2_eq));  // open: en
  and and_2 (and_2_out, not_1_out, not_2_out);
  Multiplexer #(.width(5)) multiplexer_2 (
    .in0({5{1'b0}}), .in1(multiplexer_1_out), .out(out_8), .sel(and_3_out));  // open: en
  and and_3 (and_3_out, and_2_out, comparator_6_eq);
  not not_3 (not_3_out, and_1_out);
  and and_4 (wrt, not_3_out, and_3_out);
  Multiplexer #(.width(32)) multiplexer_3 (
    .in0(alu_out), .in1(dm_out), .out(out_9), .sel(comparator_3_eq));  // open: en
endmodule
