// Logisim project oldVersion.circ as structural Verilog: 17 circuits, main circuit CPU
module CPU (
  input  Reset,
  output [31:0] instr,
  output RegWrite,
  output [4:0] RegAddr,
  output [31:0] RegData,
  output MemWrite,
  output [4:0] MemAddr,
  output [31:0] MemData
);

  wire [1:0] grf_wdata, grf_wreg, pc_src;
  wire [2:0] jump_type;
  wire [3:0] alu_op;
  wire [4:0] rd_id, rs_id, rt_id, shamt;
  wire [5:0] func, op;
  wire [15:0] imm16;
  wire [23:0] cmp_out, mem_addr, npc_out, pc, pc4_out, shifter_1_out;
  wire [25:0] imm26;
  wire [31:0] alu_out, bit_extender_2_out, dm_out, rs;

  // Probe on nothing
  CMP CMP (.A(rs), .B(MemData), .jump_type(jump_type), .pc(pc), .imm16(imm16), .cmp_out(cmp_out));
  Multiplexer #(.select(2), .width(5), .enable("false")) multiplexer_1 (
    .in0(rd_id), .in1(rt_id), .in2({5{1'b1}}), .out(RegAddr), .sel(grf_wreg));  // open: in3
  Bit_Extender #(.in_width(32), .out_width(24)) bit_extender_1 (.in(alu_out), .out(mem_addr));
  DM DM (.address(mem_addr), .write_data(MemData), .mem_write(MemWrite), .read_data(dm_out), .Reset(Reset));
  Multiplexer #(.select(2), .width(32), .enable("false")) multiplexer_2 (
    .in0(alu_out), .in1(dm_out), .in2(bit_extender_2_out), .out(RegData), .sel(grf_wdata));  // open: in3
  GRF GRF (
    .read_reg1(rs_id), .read_reg2(rt_id), .write_reg(RegAddr), .read_data1(rs), .read_data2(MemData),
    .write_data(RegData), .grf_wrt(RegWrite), .reset(Reset));
  assign bit_extender_2_out = {{8{1'b0}}, pc4_out};  // Bit_Extender bit_extender_2
  NPC NPC (.pc(pc), .imm26(imm26), .grf(rs), .cmp_npc(cmp_out), .pc_src(pc_src), .npc(npc_out));
  Shifter #(.width(24), .shift("lr")) shifter_1 (.in(mem_addr), .\dist (5'b00010), .out(shifter_1_out));
  Bit_Extender #(.in_width(24), .out_width(5)) bit_extender_3 (.in(shifter_1_out), .out(MemAddr));
  ALU ALU (.A(rs), .alu_op(alu_op), .B(MemData), .out_6(alu_out), .shamt(shamt), .imm16(imm16));
  // Probe on npc_out
  CU CU (
    .op(op), .func(func), .instr(instr), .pc_src(pc_src), .alu_op(alu_op), .grf_wreg(grf_wreg),
    .grf_wdata(grf_wdata), .grf_wrt(RegWrite), .mem_write(MemWrite), .jump_type(jump_type));
  IFU IFU (
    .npc(npc_out), .func(func), .op(op), .rs(rs_id), .rt(rt_id), .rd(rd_id), .shamt(shamt), .pc(pc),
    .imm26(imm26), .imm16(imm16), .Reset(Reset), .instr(instr));
  PC4 PC4 (.pc(pc), .pc4_out(pc4_out));

  // Other names for the same wires on the sheet: grf_wrt = RegWrite; mem_write = MemWrite; rt[31:0] = MemData
endmodule

module GRF (
  input  [4:0] read_reg1,
  input  [4:0] read_reg2,
  input  [31:0] write_data,
  input  [4:0] write_reg,
  input  grf_wrt,
  input  reset,
  output [31:0] read_data1,
  output [31:0] read_data2
);

  wire clk, R0en, R1en, R2en, R3en, R4en, R5en, R6en, R7en, R8en, R9en, R10en, R11en, R12en, R13en, R14en,
       R15en, R16en, R17en, R18en, R19en, R20en, R21en, R22en, R23en, R24en, R25en, R26en, R27en, R28en,
       R29en, R30en, R31en;
  wire [31:0] R0in, R1in, R1out, R2in, R2out, R3in, R3out, R4in, R4out, R5in, R5out, R6in, R6out, R7in,
       R7out, R8in, R8out, R9in, R9out, R10in, R10out, R11in, R11out, R12in, R12out, R13in, R13out, R14in,
       R14out, R15in, R15out, R16in, R16out, R17in, R17out, R18in, R18out, R19in, R19out, R20in, R20out,
       R21in, R21out, R22in, R22out, R23in, R23out, R24in, R24out, R25in, R25out, R26in, R26out, R27in,
       R27out, R28in, R28out, R29in, R29out, R30in, R30out, R31in, R31out;

  Register #(.width(32)) register_1 (.D(R0in), .clk(clk), .clr(reset));  // open: en, Q
  Register #(.width(32)) register_2 (.D(R2in), .Q(R2out), .clk(clk), .clr(reset));  // open: en
  Register #(.width(32)) register_3 (.D(R4in), .Q(R4out), .clk(clk), .clr(reset));  // open: en
  Register #(.width(32)) register_4 (.D(R6in), .Q(R6out), .clk(clk), .clr(reset));  // open: en
  Register #(.width(32)) register_5 (.D(R8in), .Q(R8out), .clk(clk), .clr(reset));  // open: en
  Register #(.width(32)) register_6 (.D(R10in), .Q(R10out), .clk(clk), .clr(reset));  // open: en
  Register #(.width(32)) register_7 (.D(R12in), .Q(R12out), .clk(clk), .clr(reset));  // open: en
  Register #(.width(32)) register_8 (.D(R14in), .Q(R14out), .clk(clk), .clr(reset));  // open: en
  Register #(.width(32)) register_9 (.D(R16in), .Q(R16out), .clk(clk), .clr(reset));  // open: en
  Register #(.width(32)) register_10 (.D(R18in), .Q(R18out), .clk(clk), .clr(reset));  // open: en
  Register #(.width(32)) register_11 (.D(R20in), .Q(R20out), .clk(clk), .clr(reset));  // open: en
  Register #(.width(32)) register_12 (.D(R22in), .Q(R22out), .clk(clk), .clr(reset));  // open: en
  Register #(.width(32)) register_13 (.D(R24in), .Q(R24out), .clk(clk), .clr(reset));  // open: en
  Register #(.width(32)) register_14 (.D(R26in), .Q(R26out), .clk(clk), .clr(reset));  // open: en
  Register #(.width(32)) register_15 (.D(R28in), .Q(R28out), .clk(clk), .clr(reset));  // open: en
  Register #(.width(32)) register_16 (.D(R30in), .Q(R30out), .clk(clk), .clr(reset));  // open: en
  Clock clock_1 (.out(clk));
  Register #(.width(32)) register_17 (.D(R1in), .Q(R1out), .clk(clk), .clr(reset));  // open: en
  Register #(.width(32)) register_18 (.D(R3in), .Q(R3out), .clk(clk), .clr(reset));  // open: en
  Register #(.width(32)) register_19 (.D(R5in), .Q(R5out), .clk(clk), .clr(reset));  // open: en
  Register #(.width(32)) register_20 (.D(R7in), .Q(R7out), .clk(clk), .clr(reset));  // open: en
  Register #(.width(32)) register_21 (.D(R9in), .Q(R9out), .clk(clk), .clr(reset));  // open: en
  Register #(.width(32)) register_22 (.D(R11in), .Q(R11out), .clk(clk), .clr(reset));  // open: en
  Register #(.width(32)) register_23 (.D(R13in), .Q(R13out), .clk(clk), .clr(reset));  // open: en
  Register #(.width(32)) register_24 (.D(R15in), .Q(R15out), .clk(clk), .clr(reset));  // open: en
  Register #(.width(32)) register_25 (.D(R17in), .Q(R17out), .clk(clk), .clr(reset));  // open: en
  Register #(.width(32)) register_26 (.D(R19in), .Q(R19out), .clk(clk), .clr(reset));  // open: en
  Register #(.width(32)) register_27 (.D(R21in), .Q(R21out), .clk(clk), .clr(reset));  // open: en
  Register #(.width(32)) register_28 (.D(R23in), .Q(R23out), .clk(clk), .clr(reset));  // open: en
  Register #(.width(32)) register_29 (.D(R25in), .Q(R25out), .clk(clk), .clr(reset));  // open: en
  Register #(.width(32)) register_30 (.D(R27in), .Q(R27out), .clk(clk), .clr(reset));  // open: en
  Register #(.width(32)) register_31 (.D(R29in), .Q(R29out), .clk(clk), .clr(reset));  // open: en
  Register #(.width(32)) register_32 (.D(R31in), .Q(R31out), .clk(clk), .clr(reset));  // open: en
  Multiplexer #(.select(5), .width(32), .enable("false")) multiplexer_1 (
    .in0({32{1'b0}}), .in1(R1out), .in2(R2out), .in3(R3out), .in4(R4out), .in5(R5out), .in6(R6out),
    .in7(R7out), .in8(R8out), .in9(R9out), .in10(R10out), .in11(R11out), .in12(R12out), .in13(R13out),
    .in14(R14out), .in15(R15out), .in16(R16out), .in17(R17out), .in18(R18out), .in19(R19out), .in20(R20out),
    .in21(R21out), .in22(R22out), .in23(R23out), .in24(R24out), .in25(R25out), .in26(R26out), .in27(R27out),
    .in28(R28out), .in29(R29out), .in30(R30out), .in31(R31out), .out(read_data1), .sel(read_reg1));
  Multiplexer #(.select(5), .width(32), .enable("false")) multiplexer_2 (
    .in0({32{1'b0}}), .in1(R1out), .in2(R2out), .in3(R3out), .in4(R4out), .in5(R5out), .in6(R6out),
    .in7(R7out), .in8(R8out), .in9(R9out), .in10(R10out), .in11(R11out), .in12(R12out), .in13(R13out),
    .in14(R14out), .in15(R15out), .in16(R16out), .in17(R17out), .in18(R18out), .in19(R19out), .in20(R20out),
    .in21(R21out), .in22(R22out), .in23(R23out), .in24(R24out), .in25(R25out), .in26(R26out), .in27(R27out),
    .in28(R28out), .in29(R29out), .in30(R30out), .in31(R31out), .out(read_data2), .sel(read_reg2));
  Demultiplexer #(.select(5), .width(32), .tristate("true")) demultiplexer_1 (
    .out0(R0in), .out1(R1in), .out2(R2in), .out3(R3in), .out4(R4in), .out5(R5in), .out6(R6in), .out7(R7in),
    .out8(R8in), .out9(R9in), .out10(R10in), .out11(R11in), .out12(R12in), .out13(R13in), .out14(R14in),
    .out15(R15in), .out16(R16in), .out17(R17in), .out18(R18in), .out19(R19in), .out20(R20in), .out21(R21in),
    .out22(R22in), .out23(R23in), .out24(R24in), .out25(R25in), .out26(R26in), .out27(R27in), .out28(R28in),
    .out29(R29in), .out30(R30in), .out31(R31in), .in(write_data), .sel(write_reg), .en(grf_wrt));
  Decoder #(.select(5), .enable("false")) decoder_1 (
    .out0(R0en), .out1(R1en), .out2(R2en), .out3(R3en), .out4(R4en), .out5(R5en), .out6(R6en), .out7(R7en),
    .out8(R8en), .out9(R9en), .out10(R10en), .out11(R11en), .out12(R12en), .out13(R13en), .out14(R14en),
    .out15(R15en), .out16(R16en), .out17(R17en), .out18(R18en), .out19(R19en), .out20(R20en), .out21(R21en),
    .out22(R22en), .out23(R23en), .out24(R24en), .out25(R25en), .out26(R26en), .out27(R27en), .out28(R28en),
    .out29(R29en), .out30(R30en), .out31(R31en), .sel(write_reg));
endmodule

module ALU (
  input  [4:0] shamt,
  input  [31:0] A,
  input  [31:0] B,
  input  [15:0] imm16,
  input  [3:0] alu_op,
  output [31:0] out_6
);

  wire comparator_1_lt, comparator_2_lt;
  wire [31:0] add_ans, addi_sign_ans, addi_unsign_ans, and_ans, andi_ans, imm16_sign, imm16_zero, or_ans,
       ori_ans, sll_ans, slt_ans, slti_ans, sra_ans, srl_ans, sub_ans;

  assign imm16_zero = {{16{1'b0}}, imm16};  // Bit_Extender bit_extender_1
  assign imm16_sign = {{16{imm16[15]}}, imm16};  // Bit_Extender bit_extender_2
  Multiplexer #(.select(4), .width(32), .enable("false")) multiplexer_1 (
    .in0(add_ans), .in1(sub_ans), .in2(and_ans), .in3(or_ans), .in4(sll_ans), .in5(slt_ans), .in6(sra_ans),
    .in7(srl_ans), .in8(addi_sign_ans), .in9({imm16_zero[15:0], {16{1'b0}}}), .in10(andi_ans),
    .in11(ori_ans), .in12(slti_ans), .in13(addi_unsign_ans), .out(out_6), .sel(alu_op));  // open: in14, in15
  Adder #(.width(32)) adder_1 (.a(A), .b(B), .out(add_ans));  // open: cin, cout
  assign and_ans = A & B;  // AND_Gate and_1, 32 bits wide
  assign or_ans = A | B;  // OR_Gate or_1, 32 bits wide
  Subtractor #(.width(32)) subtractor_1 (.a(A), .b(B), .out(sub_ans));  // open: bin, bout
  Shifter #(.width(32)) shifter_1 (.in(B), .\dist (shamt), .out(sll_ans));
  Shifter #(.width(32), .shift("ar")) shifter_2 (.in(B), .\dist (shamt), .out(sra_ans));
  Shifter #(.width(32), .shift("lr")) shifter_3 (.in(B), .\dist (shamt), .out(srl_ans));
  Comparator #(.width(32)) comparator_1 (.a(A), .b(B), .lt(comparator_1_lt));  // open: gt, eq
  assign slt_ans = {{31{1'b0}}, comparator_1_lt};  // Bit_Extender bit_extender_3
  Adder #(.width(32)) adder_2 (.a(A), .b(imm16_sign), .out(addi_sign_ans));  // open: cin, cout
  assign andi_ans = A & imm16_zero;  // AND_Gate and_2, 32 bits wide
  assign ori_ans = A | imm16_zero;  // OR_Gate or_2, 32 bits wide
  Comparator #(.width(32)) comparator_2 (.a(A), .b(imm16_sign), .lt(comparator_2_lt));  // open: gt, eq
  assign slti_ans = {{31{1'b0}}, comparator_2_lt};  // Bit_Extender bit_extender_4
  Adder #(.width(32)) adder_3 (.a(A), .b(imm16_zero), .out(addi_unsign_ans));  // open: cin, cout

  // Other names for the same wires on the sheet: lui_ans[31:16] = imm16_zero[15:0]
endmodule

module DM (
  input  [23:0] address,
  input  [31:0] write_data,
  input  mem_write,
  input  Reset,
  output [31:0] read_data
);

  wire and_1_out, clock_1_out;

  Clock clock_1 (.out(clock_1_out));
  and and_1 (and_1_out, clock_1_out, mem_write);
  RAM #(.addrWidth(24), .dataWidth(32), .bus("separate")) ram_1 (
    .addr(address), .din(write_data), .data(read_data), .clk(and_1_out), .clr(Reset));  // open: str, sel, ld
endmodule

module IFU (
  input  [23:0] npc,
  input  Reset,
  output [23:0] pc,
  output [31:0] instr,
  output [5:0] func,
  output [5:0] op,
  output [4:0] rs,
  output [4:0] rt,
  output [4:0] rd,
  output [25:0] imm26,
  output [4:0] shamt,
  output [15:0] imm16
);

  wire clock_1_out, comparator_1_eq;
  wire [23:0] register_1_q, shifter_1_out, subtractor_1_out;

  Clock clock_1 (.out(clock_1_out));
  Subtractor #(.width(24)) subtractor_1 (.a(pc), .b(24'h3000), .out(subtractor_1_out));  // open: bin, bout
  Register #(.width(24)) register_1 (.D(npc), .Q(register_1_q), .clk(clock_1_out), .clr(Reset));  // open: en
  Comparator #(.width(24), .mode("unsigned")) comparator_1 (
    .a(register_1_q), .b({24{1'b0}}), .eq(comparator_1_eq));  // open: gt, lt
  Shifter #(.width(24), .shift("lr")) shifter_1 (.in(subtractor_1_out), .\dist (5'b00010), .out(shifter_1_out));
  Multiplexer #(.width(24), .enable("false")) multiplexer_1 (
    .in0(register_1_q), .in1(24'h3000), .out(pc), .sel(comparator_1_eq));
  ROM #(.addrWidth(24), .dataWidth(32)) rom_1 (
    .addr(shifter_1_out), .data({instr[31:26], imm26[25:16], imm16[15:6], func}));  // open: sel

  assign imm16[5:0] = func;
  assign imm26[15:0] = {imm16[15:6], func};
  assign instr[25:0] = {imm26[25:16], imm16[15:6], func};
  assign op = instr[31:26];
  assign rd = imm16[15:11];
  assign rs = imm26[25:21];
  assign rt = imm26[20:16];
  assign shamt = imm16[10:6];

  // Other names for the same wires on the sheet: instruction[31:0] = {instr[31:26], imm26[25:16], imm16[15:6], func}

  // Notes on the sheet:
  //   contents of rom_1 (hex, n*v repeats v):
  //   341c0000 341d0000 34013456 210820 8c010004 ac010004 3c027878 411822 3c051234 34040005 0 ac85ffff
  //   8c83ffff 10650001 1000000d 34670404 10e3000b 0 3c087777 3508ffff 80022 34001100 e65020 34080000
  //   34090001 340a0001 10a4020 1109fffe 1000ffff
endmodule

module CU (
  input  [5:0] op,
  input  [5:0] func,
  input  [31:0] instr,
  output mem_write,
  output [2:0] jump_type,
  output [1:0] pc_src,
  output [3:0] alu_op,
  output [1:0] grf_wreg,
  output [1:0] grf_wdata,
  output grf_wrt
);

  CU_pc_src cu_pc_src_1 (.op(op), .func(func), .pc_src(pc_src));
  CU_alu_op cu_alu_op_1 (.op(op), .func(func), .alu_op(alu_op));
  CU_grf_wreg cu_grf_wreg_1 (.op(op), .func(func), .grf_wreg(grf_wreg));
  CU_grf_wdata cu_grf_wdata_1 (.op(op), .func(func), .grf_wreg(grf_wdata));
  CU_grf_wrt cu_grf_wrt_1 (.op(op), .func(func), .instr(instr), .grf_wrt(grf_wrt));
  CU_mem_write cu_mem_write_1 (.op(op), .mem_write(mem_write));
  CU_jump_type cu_jump_type_1 (.out_1(jump_type));
endmodule

module CMP (
  input  [31:0] A,
  input  [31:0] B,
  input  [2:0] jump_type,
  input  [23:0] pc,
  input  [15:0] imm16,
  output [23:0] cmp_out
);

  wire A_0, A_0_t, A__0, A__0_t, A__B, A_B, comparator_2_eq, multiplexer_1_out;
  wire [23:0] bit_extender_1_out, pc_4, pc_4_sign;

  Comparator #(.width(32)) comparator_1 (.a(A), .b(B), .eq(A_B));  // open: gt, lt
  Comparator #(.width(32)) comparator_2 (.a(A), .b({32{1'b0}}), .gt(A_0_t), .eq(comparator_2_eq), .lt(A_0));
  not not_1 (A__B, A_B);
  or or_1 (A__0_t, A_0_t, comparator_2_eq);
  or or_2 (A__0, comparator_2_eq, A_0);
  Adder #(.width(24)) adder_1 (.a(pc), .b(24'h4), .out(pc_4));  // open: cin, cout
  assign bit_extender_1_out = {{6{imm16[15]}}, {imm16, 2'b00}};  // Bit_Extender bit_extender_1
  // Probe on pc_4
  Adder #(.width(24)) adder_2 (.a(pc_4), .b(bit_extender_1_out), .out(pc_4_sign));  // open: cin, cout
  Multiplexer #(.select(3), .enable("false")) multiplexer_1 (
    .in0(A_B), .in1(A__0_t), .in2(A_0_t), .in3(A__0), .in4(A_0), .in5(A__B), .out(multiplexer_1_out),
    .sel(jump_type));  // open: in6, in7
  Multiplexer #(.width(24), .enable("false")) multiplexer_2 (
    .in0(pc_4), .in1(pc_4_sign), .out(cmp_out), .sel(multiplexer_1_out));
endmodule

module NPC (
  input  [23:0] pc,
  input  [25:0] imm26,
  input  [31:0] grf,
  input  [23:0] cmp_npc,
  input  [1:0] pc_src,
  output [23:0] npc
);

  wire [23:0] pc_src_00, pc_src_10;
  wire [23:2] pc_src_01;

  Multiplexer #(.select(2), .width(24), .enable("false")) multiplexer_1 (
    .in0(pc_src_00), .in1({pc_src_01, 2'b00}), .in2(pc_src_10), .in3(cmp_npc), .out(npc), .sel(pc_src));
  Adder #(.width(24)) adder_1 (.a(pc), .b(24'h4), .out(pc_src_00));  // open: cin, cout
  Bit_Extender #(.in_width(26), .out_width(22)) bit_extender_1 (.in(imm26), .out(pc_src_01));
  Bit_Extender #(.in_width(32), .out_width(24)) bit_extender_2 (.in(grf), .out(pc_src_10));

  // Other names for the same wires on the sheet: pc_src_11[23:0] = cmp_npc
endmodule

module PC4 (
  input  [23:0] pc,
  output [23:0] pc4_out
);

  Adder #(.width(24)) adder_1 (.a(24'h4), .b(pc), .out(pc4_out));  // open: cin, cout
endmodule

module CU_pc_src (
  input  [5:0] op,
  input  [5:0] func,
  output [1:0] pc_src
);

  wire and_1_out, comparator_1_eq, comparator_2_eq, comparator_3_eq, comparator_4_eq, comparator_5_eq;
  wire [1:0] multiplexer_1_out, multiplexer_2_out, multiplexer_3_out;

  Comparator #(.width(6)) comparator_1 (.a(op), .b(6'b000100), .eq(comparator_1_eq));  // open: gt, lt
  Multiplexer #(.width(2), .enable("false")) multiplexer_1 (
    .in0(2'b00), .in1(2'b11), .out(multiplexer_1_out), .sel(comparator_1_eq));
  Comparator #(.width(6)) comparator_2 (.a(func), .b(6'b001000), .eq(comparator_2_eq));  // open: gt, lt
  Comparator #(.width(6)) comparator_3 (.a(op), .b({6{1'b0}}), .eq(comparator_3_eq));  // open: gt, lt
  Multiplexer #(.width(2), .enable("false")) multiplexer_2 (
    .in0(multiplexer_1_out), .in1(2'b01), .out(multiplexer_2_out), .sel(comparator_4_eq));
  Comparator #(.width(6)) comparator_4 (.a(op), .b(6'b000011), .eq(comparator_4_eq));  // open: gt, lt
  and and_1 (and_1_out, comparator_2_eq, comparator_3_eq);
  Multiplexer #(.width(2), .enable("false")) multiplexer_3 (
    .in0(multiplexer_2_out), .in1(2'b10), .out(multiplexer_3_out), .sel(and_1_out));
  Comparator #(.width(6)) comparator_5 (.a(op), .b(6'b000010), .eq(comparator_5_eq));  // open: gt, lt
  Multiplexer #(.width(2), .enable("false")) multiplexer_4 (
    .in0(multiplexer_3_out), .in1(2'b01), .out(pc_src), .sel(comparator_5_eq));
endmodule

module CU_alu_op (
  input  [5:0] op,
  input  [5:0] func,
  output [3:0] alu_op
);

  wire comparator_1_eq, comparator_2_eq, comparator_3_eq, comparator_4_eq, comparator_5_eq, comparator_6_eq,
       comparator_7_eq, comparator_8_eq, comparator_9_eq, comparator_10_eq, comparator_11_eq,
       comparator_12_eq, comparator_13_eq;
  wire [3:0] multiplexer_1_out, multiplexer_2_out, multiplexer_3_out, multiplexer_4_out, multiplexer_5_out,
       multiplexer_6_out, multiplexer_7_out, multiplexer_9_out, multiplexer_10_out, multiplexer_11_out,
       part_false, part_true;

  Comparator #(.width(6)) comparator_1 (.a(func), .b(6'b100100), .eq(comparator_1_eq));  // open: gt, lt
  Multiplexer #(.width(4), .enable("false")) multiplexer_1 (
    .in0(4'b0000), .in1(4'b0010), .out(multiplexer_1_out), .sel(comparator_1_eq));
  Comparator #(.width(6)) comparator_2 (.a(op), .b(6'b101011), .eq(comparator_2_eq));  // open: gt, lt
  Multiplexer #(.width(4), .enable("false")) multiplexer_2 (
    .in0(4'b0000), .in1(4'b1000), .out(multiplexer_2_out), .sel(comparator_2_eq));
  Multiplexer #(.width(4), .enable("false")) multiplexer_3 (
    .in0(multiplexer_1_out), .in1(4'b0011), .out(multiplexer_3_out), .sel(comparator_3_eq));
  Comparator #(.width(6)) comparator_3 (.a(func), .b(6'b100101), .eq(comparator_3_eq));  // open: gt, lt
  Multiplexer #(.width(4), .enable("false")) multiplexer_4 (
    .in0(multiplexer_2_out), .in1(4'b1000), .out(multiplexer_4_out), .sel(comparator_4_eq));
  Comparator #(.width(6)) comparator_4 (.a(op), .b(6'b100011), .eq(comparator_4_eq));  // open: gt, lt
  Comparator #(.width(6)) comparator_5 (.a(func), .b(6'b100011), .eq(comparator_5_eq));  // open: gt, lt
  Multiplexer #(.width(4), .enable("false")) multiplexer_5 (
    .in0(multiplexer_3_out), .in1(4'b0001), .out(multiplexer_5_out), .sel(comparator_5_eq));
  Comparator #(.width(6)) comparator_6 (.a(op), .b(6'b001111), .eq(comparator_6_eq));  // open: gt, lt
  Multiplexer #(.width(4), .enable("false")) multiplexer_6 (
    .in0(multiplexer_4_out), .in1(4'b1001), .out(multiplexer_6_out), .sel(comparator_6_eq));
  Comparator #(.width(6)) comparator_7 (.a(op), .b({6{1'b0}}), .eq(comparator_7_eq));  // open: gt, lt
  Comparator #(.width(6)) comparator_8 (.a(func), .b(6'b100010), .eq(comparator_8_eq));  // open: gt, lt
  Multiplexer #(.width(4), .enable("false")) multiplexer_7 (
    .in0(multiplexer_6_out), .in1(4'b1011), .out(multiplexer_7_out), .sel(comparator_9_eq));
  Comparator #(.width(6)) comparator_9 (.a(op), .b(6'b001101), .eq(comparator_9_eq));  // open: gt, lt
  Multiplexer #(.width(4), .enable("false")) multiplexer_8 (
    .in0(part_false), .in1(part_true), .out(alu_op), .sel(comparator_7_eq));
  Comparator #(.width(6)) comparator_10 (.a(func), .b(6'b100001), .eq(comparator_10_eq));  // open: gt, lt
  Multiplexer #(.width(4), .enable("false")) multiplexer_9 (
    .in0(multiplexer_5_out), .in1(4'b0001), .out(multiplexer_9_out), .sel(comparator_8_eq));
  Comparator #(.width(6)) comparator_11 (.a(op), .b(6'b001100), .eq(comparator_11_eq));  // open: gt, lt
  Multiplexer #(.width(4), .enable("false")) multiplexer_10 (
    .in0(multiplexer_9_out), .in1(4'b0000), .out(multiplexer_10_out), .sel(comparator_10_eq));
  Comparator #(.width(6)) comparator_12 (.a(func), .b(6'b100000), .eq(comparator_12_eq));  // open: gt, lt
  Multiplexer #(.width(4), .enable("false")) multiplexer_11 (
    .in0(multiplexer_7_out), .in1(4'b1010), .out(multiplexer_11_out), .sel(comparator_11_eq));
  Comparator #(.width(6)) comparator_13 (.a(op), .b(6'b001000), .eq(comparator_13_eq));  // open: gt, lt
  Multiplexer #(.width(4), .enable("false")) multiplexer_12 (
    .in0(multiplexer_10_out), .in1(4'b0000), .out(part_true), .sel(comparator_12_eq));
  Multiplexer #(.width(4), .enable("false")) multiplexer_13 (
    .in0(multiplexer_11_out), .in1(4'b1000), .out(part_false), .sel(comparator_13_eq));
endmodule

module CU_grf_wreg (
  input  [5:0] op,
  input  [5:0] func,
  output [1:0] grf_wreg
);

  wire comparator_1_eq, comparator_2_eq, comparator_3_eq, comparator_4_eq, comparator_5_eq, comparator_6_eq,
       comparator_7_eq;
  wire [1:0] multiplexer_1_out, multiplexer_2_out, multiplexer_3_out, multiplexer_4_out, multiplexer_5_out,
       multiplexer_6_out;

  Multiplexer #(.width(2), .enable("false")) multiplexer_1 (
    .in0(2'b00), .in1(2'b10), .out(multiplexer_1_out), .sel(comparator_1_eq));
  Comparator #(.width(6)) comparator_1 (.a(op), .b(6'b000011), .eq(comparator_1_eq));  // open: gt, lt
  Comparator #(.width(6)) comparator_2 (.a(op), .b(6'b100011), .eq(comparator_2_eq));  // open: gt, lt
  Multiplexer #(.width(2), .enable("false")) multiplexer_2 (
    .in0(multiplexer_1_out), .in1(2'b01), .out(multiplexer_2_out), .sel(comparator_2_eq));
  Comparator #(.width(6)) comparator_3 (.a(op), .b(6'b001111), .eq(comparator_3_eq));  // open: gt, lt
  Comparator #(.width(6)) comparator_4 (.a(op), .b(6'b001101), .eq(comparator_4_eq));  // open: gt, lt
  Multiplexer #(.width(2), .enable("false")) multiplexer_3 (
    .in0(multiplexer_2_out), .in1(2'b01), .out(multiplexer_3_out), .sel(comparator_3_eq));
  Multiplexer #(.width(2), .enable("false")) multiplexer_4 (
    .in0(multiplexer_3_out), .in1(2'b01), .out(multiplexer_4_out), .sel(comparator_4_eq));
  Comparator #(.width(6)) comparator_5 (.a(op), .b(6'b001100), .eq(comparator_5_eq));  // open: gt, lt
  Multiplexer #(.width(2), .enable("false")) multiplexer_5 (
    .in0(multiplexer_4_out), .in1(2'b01), .out(multiplexer_5_out), .sel(comparator_5_eq));
  Comparator #(.width(6)) comparator_6 (.a(op), .b(6'b001000), .eq(comparator_6_eq));  // open: gt, lt
  Multiplexer #(.width(2), .enable("false")) multiplexer_6 (
    .in0(multiplexer_5_out), .in1(2'b01), .out(multiplexer_6_out), .sel(comparator_6_eq));
  Multiplexer #(.width(2), .enable("false")) multiplexer_7 (
    .in0(multiplexer_6_out), .in1(2'b00), .out(grf_wreg), .sel(comparator_7_eq));
  Comparator #(.width(6)) comparator_7 (.a(op), .b({6{1'b0}}), .eq(comparator_7_eq));  // open: gt, lt
endmodule

module CU_grf_wdata (
  input  [5:0] op,
  input  [5:0] func,
  output [1:0] grf_wreg
);

  wire comparator_1_eq, comparator_2_eq;
  wire [1:0] multiplexer_1_out;

  Comparator #(.width(6)) comparator_1 (.a(op), .b(6'b000011), .eq(comparator_1_eq));  // open: gt, lt
  Multiplexer #(.width(2), .enable("false")) multiplexer_1 (
    .in0(2'b00), .in1(2'b10), .out(multiplexer_1_out), .sel(comparator_1_eq));
  Comparator #(.width(6)) comparator_2 (.a(op), .b(6'b100011), .eq(comparator_2_eq));  // open: gt, lt
  Multiplexer #(.width(2), .enable("false")) multiplexer_2 (
    .in0(multiplexer_1_out), .in1(2'b01), .out(grf_wreg), .sel(comparator_2_eq));
endmodule

module CU_grf_wrt (
  input  [5:0] op,
  input  [5:0] func,
  input  [31:0] instr,
  output grf_wrt
);

  wire comparator_1_eq, comparator_2_eq, comparator_3_eq, comparator_4_eq, comparator_5_eq, comparator_6_eq,
       comparator_7_eq, not_1_out, or_1_out;

  Comparator #(.width(6), .mode("unsigned")) comparator_1 (
    .a(op), .b({6{1'b0}}), .eq(comparator_1_eq));  // open: gt, lt
  Comparator #(.width(6), .mode("unsigned")) comparator_2 (
    .a(op), .b(6'b001000), .eq(comparator_2_eq));  // open: gt, lt
  Comparator #(.width(6), .mode("unsigned")) comparator_3 (
    .a(op), .b(6'b001100), .eq(comparator_3_eq));  // open: gt, lt
  Comparator #(.width(6), .mode("unsigned")) comparator_4 (
    .a(op), .b(6'b001101), .eq(comparator_4_eq));  // open: gt, lt
  Comparator #(.width(6), .mode("unsigned")) comparator_5 (
    .a(op), .b(6'b100011), .eq(comparator_5_eq));  // open: gt, lt
  Comparator #(.width(6), .mode("unsigned")) comparator_6 (
    .a(op), .b(6'b001111), .eq(comparator_6_eq));  // open: gt, lt
  not not_1 (not_1_out, comparator_7_eq);
  Comparator #(.width(32)) comparator_7 (.a(instr), .b({32{1'b0}}), .eq(comparator_7_eq));  // open: gt, lt
  or or_1 (or_1_out, comparator_1_eq, comparator_2_eq, comparator_3_eq, comparator_4_eq, comparator_5_eq, comparator_6_eq);
  and and_1 (grf_wrt, not_1_out, or_1_out);
endmodule

module CU_mem_write (
  input  [5:0] op,
  output mem_write
);

  Comparator #(.width(6), .mode("unsigned")) comparator_1 (.a(op), .b(6'b101011), .eq(mem_write));  // open: gt, lt
endmodule

module CU_jump_type (
  output [2:0] out_1
);


  assign out_1 = 3'b000;
endmodule

module main (
  input  Reset,
  output [31:0] out_2,
  output out_3,
  output [4:0] out_4,
  output [31:0] out_5,
  output out_6,
  output [4:0] out_7,
  output [31:0] out_8
);

  CPU cpu_1 (
    .Reset(Reset), .instr(out_2), .RegWrite(out_3), .RegAddr(out_4), .RegData(out_5), .MemWrite(out_6),
    .MemAddr(out_7), .MemData(out_8));
  Clock clock_1 ();  // open: out

  // Other names for the same wires on the sheet: instr[31:0] = out_2; MemAddr[4:0] = out_7; MemData[31:0] = out_8;
  //   MemWrite = out_6; RegAddr[4:0] = out_4; RegData[31:0] = out_5; RegWrite = out_3
endmodule
